// Logisim project 12 bit register.circ as structural Verilog: 1 circuit, main circuit main
module main (
  input  LD,
  input  [11:0] Input,
  input  INC,
  input  CLR,
  input  clock,
  output [11:0] Output
);

  Counter #(.width(12), .max('hfff)) counter_1 (
    .load(LD), .D(Input), .count(INC), .Q(Output), .clk(clock), .clr(CLR));  // open: carry
endmodule
