// Logisim project 16  bit Register.circ as structural Verilog: 1 circuit, main circuit main
module main (
  input  LD,
  input  [15:0] Input,
  input  INR,
  input  CLR,
  input  clock,
  output [15:0] Output
);

  Counter #(.width(16), .max('hffff)) counter_1 (
    .load(LD), .D(Input), .count(INR), .Q(Output), .clk(clock), .clr(CLR));  // open: carry
endmodule
