// Logisim project CU.circ as structural Verilog: 1 circuit, main circuit main
module main (
  input  R,
  input  IEN,
  input  FGO,
  input  FGI,
  input  I,
  input  D0,
  input  D1,
  input  D2,
  input  D3,
  input  D4,
  input  D5,
  input  D6,
  input  D7,
  input  T0,
  input  T1,
  input  T2,
  input  T3,
  input  T4,
  input  T5,
  input  T6,
  input  B0,
  input  B1,
  input  B2,
  input  B3,
  input  B4,
  input  B5,
  input  B6,
  input  B7,
  input  B8,
  input  B9,
  input  B10,
  input  B11,
  output MR,
  output MW,
  output LOAD_AC,
  output INC_AC,
  output CLR_AC,
  output LOAD_AR,
  output INR_AR,
  output CLR_AR,
  output LOAD_PC,
  output INR_PC,
  output CLR_PC,
  output LOAD_DR,
  output INC_DR,
  output LOAD_IR,
  output LOAD_TR,
  output LOAD_OUTR,
  output FGO_2,
  output FGI_2,
  output IEN_1,
  output IEN_0,
  output I_2,
  output S,
  output R_1,
  output R_0,
  output E,
  output SC,
  output [6:0] ACCU
);

  wire and_1_out, and_2_out, and_3_out, and_4_out, and_5_out, and_6_out, and_7_out, and_8_out, and_10_out,
       and_11_out, and_12_out, and_15_out, and_16_out, and_17_out, and_18_out, and_19_out, and_20_out,
       and_21_out, and_22_out, and_23_out, and_24_out, and_25_out, and_27_out, and_28_out, and_29_out,
       and_30_out, and_36_out, and_37_out, and_38_out, and_39_out, and_40_out, and_41_out, and_42_out,
       and_43_out, and_44_out, and_45_out, and_46_out, and_47_out, and_48_out, and_49_out, and_50_out,
       not_1_out, not_2_out, not_3_out, not_4_out, not_5_out, not_6_out, not_7_out, or_1_out, or_2_out,
       or_3_out;

  not not_1 (not_1_out, I);
  and and_1 (and_1_out, D7, not_1_out, T3);
  and and_2 (and_2_out, D7, I, T3);
  not not_2 (not_2_out, T1);
  not not_3 (not_3_out, T2);
  not not_4 (not_4_out, T0);
  or or_1 (or_1_out, D0, D1, D2, D6);
  or or_2 (or_2_out, D3, D5);
  not not_5 (not_5_out, R);
  not not_6 (not_6_out, D7);
  and and_3 (and_3_out, not_5_out, T1);
  and and_4 (and_4_out, not_6_out, I, T3);
  and and_5 (and_5_out, or_1_out, T4);
  and and_6 (and_6_out, or_2_out, T4);
  and and_7 (and_7_out, D6, T6);
  and and_8 (and_8_out, R, T1);
  and AND_9 (ACCU[0], D0, T5);
  and ADD (ACCU[1], D1, T5);
  and DDR (ACCU[2], D2, T5);
  and INPR (ACCU[3], and_2_out, B11);
  and COM (ACCU[4], and_1_out, B9);
  and SHR (ACCU[5], and_1_out, B7);
  and SHL (ACCU[6], and_1_out, B7);
  and INC (INC_AC, and_1_out, B5);
  and CLR (CLR_AC, and_1_out, B11);
  and and_10 (and_10_out, not_6_out, I, T3);
  not not_7 (not_7_out, R);
  and and_11 (and_11_out, not_7_out, T2);
  and and_12 (and_12_out, not_7_out, T0);
  and and_13 (INR_AR, D5, T4);
  and and_14 (CLR_AR, T0, R);
  and and_15 (and_15_out, D4, T4);
  and and_16 (and_16_out, D5, T5);
  and and_17 (and_17_out, not_7_out, T1);
  and and_18 (and_18_out, D6, T6);
  and and_19 (and_19_out, and_1_out, B4);
  and and_20 (and_20_out, and_1_out, B3);
  and and_21 (and_21_out, and_1_out, B2);
  and and_22 (and_22_out, and_1_out, B1);
  and and_23 (and_23_out, and_2_out, B9);
  and and_24 (and_24_out, and_2_out, B8);
  and and_25 (and_25_out, R, T2);
  and and_26 (CLR_PC, R, T1);
  and and_27 (and_27_out, D0, T4);
  and and_28 (and_28_out, D1, T4);
  and and_29 (and_29_out, D2, T4);
  and and_30 (and_30_out, D6, T4);
  and and_31 (INC_DR, D6, T5);
  and and_32 (LOAD_IR, not_7_out, T1);
  and and_33 (LOAD_TR, R, T0);
  and and_34 (LOAD_OUTR, and_2_out, B10);
  and u_FGO (FGO_2, and_2_out, B10);
  and u_FGI (FGI_2, and_2_out, B11);
  and and_35 (IEN_1, and_2_out, B7);
  and and_36 (and_36_out, and_2_out, B6);
  and and_37 (and_37_out, R, T2);
  and u_I (I_2, not_7_out, T2);
  and u_S (S, and_1_out, B0);
  and and_38 (and_38_out, D1, T5);
  and and_39 (and_39_out, and_1_out, B10);
  and and_40 (and_40_out, and_1_out, B8);
  and and_41 (and_41_out, and_1_out, B7);
  and and_42 (and_42_out, and_1_out, B6);
  and and_43 (and_43_out, R, T2);
  and and_44 (and_44_out, D0, T5);
  and and_45 (and_45_out, D1, T5);
  and and_46 (and_46_out, D2, T5);
  and and_47 (and_47_out, D3, T4);
  and and_48 (and_48_out, D4, T4);
  and and_49 (and_49_out, D5, T5);
  and and_50 (and_50_out, D6, T6);
  or or_3 (or_3_out, FGI, FGO);
  or or_4 (MR, and_3_out, and_4_out, and_5_out);
  or or_5 (MW, and_6_out, and_7_out, and_8_out);
  and and_51 (R_1, or_3_out, IEN, not_2_out, not_3_out, not_4_out);
  and and_52 (R_0, R, T2);
  or or_6 (LOAD_AC, ACCU[0], ACCU[1], ACCU[2], ACCU[3], ACCU[4], ACCU[5], ACCU[6]);
  or or_7 (LOAD_AR, and_10_out, and_11_out, and_12_out);
  or or_8 (LOAD_PC, and_15_out, and_16_out);
  or or_9 (INR_PC, and_17_out, and_18_out, and_19_out, and_20_out, and_21_out, and_22_out, and_23_out, and_24_out, and_25_out);
  or or_10 (LOAD_DR, and_27_out, and_28_out, and_29_out, and_30_out);
  or or_11 (IEN_0, and_36_out, and_37_out);
  or or_12 (E, and_38_out, and_39_out, and_40_out, and_41_out, and_42_out);
  or or_13 (SC, and_43_out, and_44_out, and_45_out, and_46_out, and_47_out, and_48_out, and_49_out, and_50_out, and_1_out, and_2_out);
endmodule
