// Logisim project INPR.circ as structural Verilog: 1 circuit, main circuit main
module main (
  input  LD,
  input  [6:0] INPUT,
  input  clock,
  input  CLR,
  output [7:0] OUTPUT
);

  wire [7:0] bit_extender_1_out;

  assign bit_extender_1_out = {{1{1'b0}}, INPUT};  // Bit_Extender bit_extender_1
  Counter counter_1 (
    .load(LD), .D(bit_extender_1_out), .count(1'b0), .Q(OUTPUT), .clk(clock), .clr(CLR));  // open: carry
endmodule
