// Logisim project MAIN ALU.circ as structural Verilog: 1 circuit, main circuit main
module main (
  input  [7:0] INPR,
  input  [15:0] AC_INPUT,
  input  _0,
  input  AND,
  input  ADD,
  input  DDR,
  input  INPR_2,
  input  COM,
  input  SHR,
  input  SHL,
  input  [15:0] DR_INPUT,
  input  FROM_E,
  output [15:0] AC_OUTPUT,
  output E_OUT
);

  wire main_1_c_out, main_1_e_in;

  Complete_ALU_main main_1 (
    .AND(AND), ._0(_0), .ADD(ADD), .DR(DDR), ._3DR(DR_INPUT[3]), .INPR(INPR_2), .COM(COM), .SHR(SHR),
    .SHL(SHL), ._0inpr(INPR[0]), ._0AC_prime(AC_OUTPUT[0]), ._4AC_prime(AC_OUTPUT[4]),
    ._8AC_prime(AC_OUTPUT[8]), ._12AC_prime(AC_OUTPUT[12]), ._1inpr(INPR[1]), ._1AC_prime(AC_OUTPUT[1]),
    ._5AC_prime(AC_OUTPUT[5]), ._9AC_prime(AC_OUTPUT[9]), ._13AC_prime(AC_OUTPUT[13]), ._2inpr(INPR[2]),
    ._2AC_prime(AC_OUTPUT[2]), ._6AC_prime(AC_OUTPUT[6]), ._10AC_prime(AC_OUTPUT[10]),
    ._14AC_prime(AC_OUTPUT[14]), ._3inpr(INPR[3]), ._3AC_prime(AC_OUTPUT[3]), ._7AC_prime(AC_OUTPUT[7]),
    ._11AC_prime(AC_OUTPUT[11]), ._15AC_prime(AC_OUTPUT[15]), .C_OUT(main_1_c_out), .FROM_E(FROM_E),
    ._0AC(AC_INPUT[0]), ._1AC(AC_INPUT[1]), ._2AC(AC_INPUT[2]), ._3AC(AC_INPUT[3]), ._0DR(DR_INPUT[0]),
    ._1DR(DR_INPUT[1]), ._2dr(DR_INPUT[2]), ._4inpr(INPR[4]), ._5inpr(INPR[5]), ._6inpr(INPR[6]),
    ._7inpr(INPR[7]), ._4AC(AC_INPUT[4]), ._5AC(AC_INPUT[5]), ._6AC(AC_INPUT[6]), ._7AC(AC_INPUT[7]),
    ._4DR(DR_INPUT[4]), ._5DR(DR_INPUT[5]), ._6DR(DR_INPUT[6]), ._7DR(DR_INPUT[7]), ._8AC(AC_INPUT[8]),
    ._9AC(AC_INPUT[9]), ._10AC(AC_INPUT[10]), ._11AC(AC_INPUT[11]), ._8DR(DR_INPUT[8]), ._9DR(DR_INPUT[9]),
    ._10DR(DR_INPUT[10]), ._11DR(DR_INPUT[11]), .E_IN(main_1_e_in), ._12AC(AC_INPUT[12]),
    ._13AC(AC_INPUT[13]), ._14AC(AC_INPUT[14]), ._15AC(AC_INPUT[15]), ._12DR(DR_INPUT[12]),
    ._13DR(DR_INPUT[13]), ._14DR(DR_INPUT[14]), ._15DR(DR_INPUT[15]));
  or or_1 (E_OUT, main_1_c_out, main_1_e_in);
endmodule
