// Logisim project MAIN PC.circ as structural Verilog: 1 circuit, main circuit main
module main (
  input  START
);

  wire CLOCK_out, E_q, FGI_q, FGO_q, I_q, IEN_q, main_1_clr_ac, main_1_clr_ar, main_1_clr_pc, main_1_e,
       main_1_fgi_2, main_1_fgo_2, main_1_i_2, main_1_ien_0, main_1_ien_1, main_1_inc_ac, main_1_inc_dr,
       main_1_inr_ar, main_1_inr_pc, main_1_load_ac, main_1_load_ar, main_1_load_dr, main_1_load_ir,
       main_1_load_outr, main_1_load_pc, main_1_load_tr, main_1_mr, main_1_mw, main_1_r_0, main_1_r_1,
       main_1_s, main_1_sc, main_2_e_out, or_1_out, R_q, S_q;
  wire [2:0] main_3_s0;
  wire [3:0] SC_a1;
  wire [6:0] decoder_2_out0, main_1_accu;
  wire [7:0] decoder_1_out0, INPR_output;
  wire [11:0] AR_output, PC_output;
  wire [15:0] AC_output, bit_extender_1_out, bit_extender_2_out, DR_output, IR_output, main_2_ac_output,
       multiplexer_1_out, ram_1_data, TR_output;

  Clock CLOCK (.out(CLOCK_out));
  LED led_1 (.in(START));
  J_K_Flip_Flop IEN (.J(main_1_ien_1), .clk(CLOCK_out), .K(main_1_ien_0), .Q(IEN_q));  // open: Qn, preset, en, reset
  COUNTER_main SC (.CLK(CLOCK_out), .Clear(main_1_sc), .Load(S_q), .A1(SC_a1));
  D_Flip_Flop I (.clk(CLOCK_out), .D(IR_output[15]), .Q(I_q));  // open: Qn, preset, en, reset
  Decoder #(.select(3), .enable("false")) decoder_1 (
    .out0(decoder_1_out0[0]), .out1(decoder_1_out0[1]), .out2(decoder_1_out0[2]), .out3(decoder_1_out0[3]),
    .out4(decoder_1_out0[4]), .out5(decoder_1_out0[5]), .out6(decoder_1_out0[6]), .out7(decoder_1_out0[7]),
    .sel(IR_output[14:12]));
  Decoder #(.select(4), .enable("false")) decoder_2 (
    .out0(decoder_2_out0[0]), .out1(decoder_2_out0[1]), .out2(decoder_2_out0[2]), .out3(decoder_2_out0[3]),
    .out4(decoder_2_out0[4]), .out5(decoder_2_out0[5]), .out6(decoder_2_out0[6]), .sel(SC_a1));  // open: out7, out8, out9, out10, out11, out12, out13, out14, out15
  J_K_Flip_Flop S (.J(START), .clk(CLOCK_out), .K(main_1_s), .Q(S_q));  // open: Qn, preset, en, reset
  D_Flip_Flop E (.clk(CLOCK_out), .D(main_2_e_out), .Q(E_q), .en(main_1_e));  // open: Qn, preset, reset
  RAM #(.addrWidth(12), .dataWidth(16), .bus("separate")) ram_1 (
    .addr(AR_output), .din(multiplexer_1_out), .data(ram_1_data), .str(main_1_mw), .sel(or_1_out),
    .clk(CLOCK_out), .ld(main_1_mr), .clr(1'b0));
  CU_main main_1 (
    .I(I_q), .D0(decoder_1_out0[0]), .D1(decoder_1_out0[1]), .D2(decoder_1_out0[2]), .D3(decoder_1_out0[3]),
    .D4(decoder_1_out0[4]), .D5(decoder_1_out0[5]), .D6(decoder_1_out0[6]), .D7(decoder_1_out0[7]),
    .T0(decoder_2_out0[0]), .T1(decoder_2_out0[1]), .T2(decoder_2_out0[2]), .T3(decoder_2_out0[3]),
    .T4(decoder_2_out0[4]), .T5(decoder_2_out0[5]), .T6(decoder_2_out0[6]), .B0(IR_output[0]),
    .B1(IR_output[1]), .B2(IR_output[2]), .B3(IR_output[3]), .B4(IR_output[4]), .B5(IR_output[5]),
    .B6(IR_output[6]), .B7(IR_output[7]), .B8(IR_output[8]), .B9(IR_output[9]), .B10(IR_output[10]),
    .B11(IR_output[11]), .R(R_q), .IEN(IEN_q), .FGO(FGO_q), .FGI(FGI_q), .ACCU(main_1_accu), .MR(main_1_mr),
    .MW(main_1_mw), .LOAD_AC(main_1_load_ac), .INC_AC(main_1_inc_ac), .CLR_AC(main_1_clr_ac),
    .LOAD_AR(main_1_load_ar), .INR_AR(main_1_inr_ar), .CLR_AR(main_1_clr_ar), .LOAD_PC(main_1_load_pc),
    .INR_PC(main_1_inr_pc), .CLR_PC(main_1_clr_pc), .LOAD_DR(main_1_load_dr), .INC_DR(main_1_inc_dr),
    .LOAD_IR(main_1_load_ir), .LOAD_TR(main_1_load_tr), .LOAD_OUTR(main_1_load_outr), .FGO_2(main_1_fgo_2),
    .FGI_2(main_1_fgi_2), .IEN_1(main_1_ien_1), .IEN_0(main_1_ien_0), .I_2(main_1_i_2), .S(main_1_s),
    .R_1(main_1_r_1), .R_0(main_1_r_0), .E(main_1_e), .SC(main_1_sc));
  INPR_main INPR (.clock(CLOCK_out), .OUTPUT(INPR_output));  // open: LD, INPUT, CLR
  or or_1 (or_1_out, main_1_mw, main_1_mr);
  MAIN_ALU_main main_2 (
    .INPR(INPR_output), .AC_INPUT(AC_output), .AC_OUTPUT(main_2_ac_output), ._0(1'b0), .AND(main_1_accu[0]),
    .ADD(main_1_accu[1]), .DDR(main_1_accu[2]), .INPR_2(main_1_accu[3]), .COM(main_1_accu[4]),
    .SHR(main_1_accu[5]), .SHL(main_1_accu[6]), .DR_INPUT(DR_output), .E_OUT(main_2_e_out), .FROM_E(E_q));
  J_K_Flip_Flop R (.J(main_1_r_1), .K(main_1_r_0), .Q(R_q));  // open: clk, Qn, preset, en, reset
  control_of_bus_main main_3 (
    .D0(decoder_1_out0[0]), .D1(decoder_1_out0[1]), .D2(decoder_1_out0[2]), .D3(decoder_1_out0[3]),
    .D4(decoder_1_out0[4]), .D5(decoder_1_out0[5]), .D6(decoder_1_out0[6]), .D7(decoder_1_out0[7]),
    .T0(decoder_2_out0[0]), .T1(decoder_2_out0[1]), .T2(decoder_2_out0[2]), .T3(decoder_2_out0[3]),
    .T4(decoder_2_out0[4]), .T5(decoder_2_out0[5]), .T6(decoder_2_out0[6]), .I(main_1_i_2), .R(R_q),
    .B10(IR_output[10]), .S0(main_3_s0[0]), .S1(main_3_s0[1]), .S2(main_3_s0[2]));
  J_K_Flip_Flop FGO (.clk(CLOCK_out), .K(main_1_fgo_2), .Q(FGO_q));  // open: J, Qn, preset, en, reset
  J_K_Flip_Flop FGI (.clk(CLOCK_out), .K(main_1_fgi_2), .Q(FGI_q));  // open: J, Qn, preset, en, reset
  assign bit_extender_1_out = {{4{1'b0}}, AR_output};  // Bit_Extender bit_extender_1
  _12_bit_register_main AR (
    .LD(main_1_load_ar), .Input(multiplexer_1_out[11:0]), .INC(main_1_inr_ar), .CLR(main_1_clr_ar),
    .clock(CLOCK_out), .Output(AR_output));
  assign bit_extender_2_out = {{4{1'b0}}, PC_output};  // Bit_Extender bit_extender_2
  _12_bit_register_main PC (
    .LD(main_1_load_pc), .Input(multiplexer_1_out[11:0]), .INC(main_1_inr_pc), .CLR(main_1_clr_pc),
    .clock(CLOCK_out), .Output(PC_output));
  _16__bit_Register_main DR (
    .LD(main_1_load_dr), .Input(multiplexer_1_out), .INR(main_1_inc_dr), .CLR(1'b0), .clock(CLOCK_out),
    .Output(DR_output));
  _16__bit_Register_main AC (
    .LD(main_1_load_ac), .Input(main_2_ac_output), .INR(main_1_inc_ac), .CLR(main_1_clr_ac),
    .clock(CLOCK_out), .Output(AC_output));
  _16__bit_Register_main IR (
    .LD(main_1_load_ir), .Input(multiplexer_1_out), .INR(1'b0), .CLR(1'b0), .clock(CLOCK_out),
    .Output(IR_output));
  _16__bit_Register_main TR (
    .LD(main_1_load_tr), .Input(multiplexer_1_out), .INR(1'b0), .CLR(1'b0), .clock(CLOCK_out),
    .Output(TR_output));
  OUTR_main OUTR (.LD(main_1_load_outr), .INPUT(multiplexer_1_out), .clock(CLOCK_out));
  Multiplexer #(.select(3), .width(16), .enable("false")) multiplexer_1 (
    .in1(bit_extender_1_out), .in2(bit_extender_2_out), .in3(DR_output), .in4(AC_output), .in5(IR_output),
    .in6(TR_output), .in7(ram_1_data), .out(multiplexer_1_out), .sel(main_3_s0));  // open: in0
endmodule
