// Logisim project OUTR.circ as structural Verilog: 1 circuit, main circuit main
module main (
  input  LD,
  input  [15:0] INPUT,
  input  clock
);

  wire [7:0] bit_extender_1_out;

  Bit_Extender #(.in_width(16), .out_width(8)) bit_extender_1 (.in(INPUT), .out(bit_extender_1_out));
  Counter counter_1 (.load(LD), .D(bit_extender_1_out), .clk(clock));  // open: count, Q, carry, clr
endmodule
