// Logisim project control of bus.circ as structural Verilog: 1 circuit, main circuit main
module main (
  input  D0,
  input  D1,
  input  D2,
  input  D3,
  input  D4,
  input  D5,
  input  D6,
  input  D7,
  input  T0,
  input  T1,
  input  T2,
  input  T3,
  input  T4,
  input  T5,
  input  T6,
  input  I,
  input  R,
  input  B10,
  output S0,
  output S1,
  output S2
);

  wire and_1_out, and_2_out, and_3_out, and_4_out, and_5_out, and_6_out, and_7_out, and_8_out, and_9_out,
       and_10_out, and_11_out, not_1_out, not_2_out, or_1_out, or_2_out, or_3_out, or_4_out, or_5_out;

  not not_1 (not_1_out, R);
  or or_1 (or_1_out, D2, D5);
  or or_2 (or_2_out, D4, D0, D1, D2, D6);
  or or_3 (or_3_out, T2, T1);
  not not_2 (not_2_out, D7);
  or or_4 (or_4_out, D5, D0, D1, D2, D6);
  or or_5 (or_5_out, D0, D1, D2, D6, D3);
  and and_1 (and_1_out, or_1_out, T5);
  and and_2 (and_2_out, or_2_out, T4);
  and and_3 (and_3_out, D6, T6);
  and and_4 (and_4_out, or_3_out, not_1_out);
  and and_5 (and_5_out, not_2_out, I, T3);
  and and_6 (and_6_out, or_4_out, T4);
  and and_7 (and_7_out, D2, T5);
  and and_8 (and_8_out, D6, T6);
  and and_9 (and_9_out, or_5_out, T4);
  and and_10 (and_10_out, not_1_out, T2);
  and and_11 (and_11_out, D7, I, T3, B10);
  or or_6 (S0, and_1_out, and_2_out, and_3_out, and_4_out, and_5_out);
  or or_7 (S1, and_5_out, T0, and_7_out, and_6_out, T1, and_8_out);
  or or_8 (S2, T1, and_9_out, and_5_out, and_11_out, and_10_out);
endmodule
